# Fritzing sketch wemos-voltage (saved by Fritzing 0.9.3b)

parts:
  WeMos_D1_Mini1 = WeMos D1 Mini
  18650_holder1 = 18650 holder [package="DIP (Dual Inline) [THT]"]
  R1 = Resistor [tolerance=±5% resistance=22 package="2512 [SMD]"]
  R2 = Resistor [tolerance=±5% resistance=100k package="2512 [SMD]"]
  microSD1 = MicroSD Card Module
  OLED_I2C1 = OLED 128x64 I2C Monochrome Display
  WeMos_D1_Mini_Battery_Shield1 = WeMos D1 Mini Battery Shield

nets:
  3V3: WeMos_D1_Mini1.3V3, OLED_I2C1.VDD
  5V: WeMos_D1_Mini1.5V, microSD1.VCC, WeMos_D1_Mini_Battery_Shield1.5V
  N1: WeMos_D1_Mini1.A0, R2.Pin_0
  N2: WeMos_D1_Mini1.D1, OLED_I2C1.SCK
  N3: WeMos_D1_Mini1.D2, OLED_I2C1.SDA
  N4: WeMos_D1_Mini1.D5, microSD1.SCK
  N5: WeMos_D1_Mini1.D6, microSD1.MISO
  N6: WeMos_D1_Mini1.D7, microSD1.MOSI
  N7: WeMos_D1_Mini1.D8, microSD1.CS
  GND: WeMos_D1_Mini1.G, microSD1.GND, OLED_I2C1.GND, WeMos_D1_Mini_Battery_Shield1.G
  N8: 18650_holder1.holder_+, R1.Pin_0, R2.Pin_1
  N9: 18650_holder1.holder_-, R1.Pin_1

notes:
  GND GND
  VCC VCC
  MISO D6
  MOSI D7
  SCK D5
  CS D8

custom parts:
  18650 holder: Акум формата 18650 в холдере
