# Fritzing sketch wemos-voltage2 (saved by Fritzing 0.9.3b)

parts:
  WeMos_D1_Mini1 = WeMos D1 Mini
  R2 = Resistor [tolerance=±5% resistance=100k package="2512 [SMD]"]
  R3 = Resistor [tolerance=±5% resistance=320k package="2512 [SMD]"]

nets:
  N1: WeMos_D1_Mini1.A0, R2.Pin_0
  N2: WeMos_D1_Mini1.G, R3.Pin_0

notes:
  Входное напряжение
