# Fritzing sketch wemos-voltage3 (saved by Fritzing 0.9.3b)

parts:
  R3 = Resistor [tolerance=±5% resistance=320k package="2512 [SMD]"]
  Часть1 = Arduino Uno (Rev3) - ICSP

nets:
  N1: R3.Pin_0, Часть1.A0
  N2: R3.Pin_1, Часть1.GND

notes:
  Входное напряжение
